# Fritzing sketch Controller (saved by Fritzing 0.9.2b)
circuit board: 8.46667cm x 5.64444cm
breadboards: 1

parts:
  Part1 = Arduino Uno (Rev3)
  M1 = DC Motor
  U6 = RELAY [package=relay-g5q]
  U7 = RELAY [package=relay-g5q]
  U8 = RELAY [package=relay-g5q]
  U9 = RELAY [package=relay-g5q]
  Orig_Motor_Output = Screw terminal - 2 pins [package=THT]
  Direct_Power_Input = Screw terminal - 2 pins [package=THT]
  U10 = RELAY [package=relay-g5q]
  U11 = RELAY [package=relay-g5q]
  Left_and_Right = Screw terminal - 2 pins [package=THT]  # not connected

nets:
  N1: Part1.D2, U6.COIL2
  N2: Part1.D3_PWM, U7.COIL2
  N3: Part1.D4, U8.COIL2
  N4: Part1.D5_PWM, U9.COIL2
  N5: Part1.D6_PWM, U10.COIL2
  N6: Part1.D7, U11.COIL2
  GND: Part1.GND, U6.COIL1, U7.COIL1, U8.COIL1, U9.NO, U9.COIL1, Direct_Power_Input.pin2, U10.COIL1, U11.COIL1
  5V: Part1.VIN
  N7: M1.pin_1, U7.MAIN
  N8: M1.pin_2, U6.MAIN
  N9: U6.NO, U7.NC, U8.MAIN
  N10: U6.NC, U7.NO, U9.MAIN
  12V: U8.NO, Direct_Power_Input.pin1
  N11: U8.NC, Orig_Motor_Output.pin1
  N12: U9.NC, Orig_Motor_Output.pin2
